# Fritzing sketch Line03 (saved by Fritzing 0.9.3b)
breadboards: 1

parts:
  Raspberry_Pi_1 = Raspberry Pi 3 [part_number=RPI-3-V1.2]
  M1 = DC Motor
  LED1 = RGB LED (com. anode, rbg) [package="5 mm [THT]"]
  LED2 = 7-SEGMENT-4DIGIT-YOUNGSUN [package=7-segment-4digit-youngsun-longpads]
  R1 = Resistor [tolerance=±5% resistance=220 package=THT]
  R2 = Resistor [tolerance=±5% resistance=220 package=THT]
  R3 = Resistor [tolerance=±5% resistance=220 package=THT]
  R4 = Resistor [tolerance=±5% resistance=220 package=THT]
  R5 = Resistor [tolerance=±5% resistance=220 package=THT]
  R6 = Resistor [tolerance=±5% resistance=220 package=THT]
  R7 = Resistor [tolerance=±5% resistance=220 package=THT]
  R8 = Resistor [tolerance=±5% resistance=220 package=THT]

nets:
  N1: Raspberry_Pi_1.GND, M1.pin_2, LED1.green_cathode
  N2: Raspberry_Pi_1.GIPO10, LED2.DIG2, R4.Pin_0, R4.Pin_1
  N3: Raspberry_Pi_1.GIPO9, LED2.D, R5.Pin_0, R5.Pin_1
  N4: Raspberry_Pi_1.GIPO11, LED2.COL-A, R6.Pin_0, R6.Pin_1
  N5: Raspberry_Pi_1.ID_SD, LED2.COL-C
  N6: Raspberry_Pi_1.GIPO5, LED2.F
  N7: Raspberry_Pi_1.GIPO6, R3.Pin_1
  N8: Raspberry_Pi_1.GIPO19, LED2.E, R8.Pin_0, R8.Pin_1
  N9: Raspberry_Pi_1.GIPO26, LED2.DIG3, R7.Pin_0, R7.Pin_1
  N10: Raspberry_Pi_1.GIPO21, LED2.DP
  N11: Raspberry_Pi_1.GIPO20, R2.Pin_1
  N12: Raspberry_Pi_1.GIPO16, R1.Pin_1
  N13: Raspberry_Pi_1.GIPO12, LED2.G
  N14: Raspberry_Pi_1.GIPO8, LED1.common_anode
  N15: Raspberry_Pi_1.GIPO25, LED1.red_cathode
  N16: Raspberry_Pi_1.5V, M1.pin_1
  N17: LED2.APOS-A, R3.Pin_0
  N18: LED2.C, R2.Pin_0
  N19: LED2.A, R1.Pin_0
